# Fritzing sketch BambuLights (saved by Fritzing 0.9.5d)
breadboards: 1

parts:
  A1 = ESP32-pico-kit-v4 [part_number=ESP32--pico-kit-v4]
  U1 = WS2812 RGB LED strip
  CD40109B1 = CD40109B level shifter [package="DIP (Dual Inline) [THT]"]

nets:
  N1: A1.Pin_10, CD40109B1.Ain
  N2: A1.Pin_18, A1.Pin_21, CD40109B1.Vcc, CD40109B1.Aen
  GND: A1.Pin_19, A1.Pin_22, U1.GND, CD40109B1.Vss
  VCC: A1.Pin_20, U1.VCC, CD40109B1.Vdd
  N3: U1.DIN, CD40109B1.Aout

custom parts:
  ESP32-pico-kit-v4: ESP32-PICO-KIT is a mini development board produced by Espressif. At the core of this board is the ESP32-PICO-D4, a System-in-Package (SiP) module with complete Wi-Fi and Bluetooth functionalities.
  WS2812 RGB LED strip: WS2812 strip
  CD40109B level shifter: A DIP stand-in part for whatever IC you want. With 16 pins on a 300mil dual inline package (DIP) footprint.
